# Fritzing sketch ESP8266 Wifi Modem (saved by Fritzing 0.9.2b)
breadboards: 1

parts:
  Bauteil1 = Arduino Uno (Rev3)
  U1 = ESP8266 WiFi Module [part_number=ESP8266]
  R1 = Resistor [tolerance=±5% resistance=1.5k package=THT]
  R2 = Resistor [tolerance=±5% resistance=1k package=THT]
  C1 = Electrolytic Capacitor [capacitance=1µF package="100 mil [THT, electrolytic]"]

nets:
  N1: Bauteil1.D0/RX, U1.TXD
  N2: Bauteil1.D1/TX, R2.Pin_0
  3V3: Bauteil1.3V3, U1.VCC, U1.CH_PD, C1.+
  GND: Bauteil1.GND, U1.GND, R1.Pin_1, C1.-
  N3: U1.RXD, R1.Pin_0, R2.Pin_1

custom parts:
  ESP8266 WiFi Module: Generic WiFi Module based on the ESP8266 with onboard PCB antenna and UART communications
