# Fritzing sketch SiKoGen (saved by Fritzing 0.9.2b)
breadboards: 1

parts:
  IC1 = 3W33DC15DC [package=DIL]
  IC2 = 3W33DC15DC [package=DIL]
  D3 = Schottky Diode [part_number=1N5817 package="300 mil [THT]"]  # not connected
  R1 = Resistor [tolerance=±5% resistance=2.2k package=THT]
  U1 = Voltage Regulator [package=to220-adj]
  R2 = Resistor [tolerance=±5% resistance=220 package=THT]
  R3 = Resistor [tolerance=±5% resistance=33 package=THT]
  LED1 = LED - 3mm [color="Blue (470nm)" package="3 mm [THT]"]
  Bauteil1 = Arduino Uno (Rev3)
  U2 = 2-Channel 5v Relay Shield [package=relay-2ch5v10a]
  J1 = female pin header, 2 pins [form="♀ (female)"]

nets:
  VIN: IC1.VIN, IC2.VIN, Bauteil1.5V, U2.VCC
  GND: IC1.GND#4, IC2.GND#4, Bauteil1.GND, U2.GND
  N1: IC1.+Vo, IC2.-Vo
  N2: IC1.-Vo, U2.K1-In
  N3: IC2.+Vo, R1.Pin_0
  N4: R1.Pin_1, U1.IN
  N5: U1.ADJ, R2.Pin_0, LED1.cathode
  N6: U1.OUT, R3.Pin_1
  N7: R2.Pin_1, R3.Pin_0
  N8: LED1.anode, U2.K2-In
  N9: Bauteil1.D2, U2.IN1
  N10: Bauteil1.D3_PWM, U2.IN2
  N11: U2.K1-Off, U2.K2-On, J1.pin1
  N12: U2.K1-On, U2.K2-Off, J1.pin2

custom parts:
  2-Channel 5v Relay Shield: 2 Channel 5v Relay Shield w. 2x SPD-06VDC-SD-C
